# Fritzing sketch DS18B20 (saved by Fritzing 0.8.7b)

parts:
  part = Electrolytic Capacitor [capacitance=1µF package="100 mil [THT, electrolytic]"]  # not connected
  Arduino_Uno_and_Ethernet_shield = Arduino Uno (Rev3)
  DS1 = DS18B20 1-Wire Temperature Sensor [part_number=DS18B20]
  R1 = Resistor [tolerance=±5% resistance=4.7k package=THT]

nets:
  N1: Arduino_Uno_and_Ethernet_shield.A0, DS1.DQ, R1.Pin_1
  GND: Arduino_Uno_and_Ethernet_shield.GND, DS1.GND
  5V: Arduino_Uno_and_Ethernet_shield.5V, DS1.VDD, R1.Pin_0
