# Fritzing sketch LM35 (saved by Fritzing 0.8.7b)

parts:
  T1_LM35DZ = LM35 Temperature Sensor [package="TO92 [THT]"]
  C1 = Electrolytic Capacitor [capacitance=10µF voltage=10V package="100 mil [THT, electrolytic]"]
  part = Electrolytic Capacitor [capacitance=1µF package="100 mil [THT, electrolytic]"]  # not connected
  Arduino_Uno_and_Ethernet_shield = Arduino Uno (Rev3)

nets:
  N1: T1_LM35DZ.+Vs, Arduino_Uno_and_Ethernet_shield.5V
  N2: T1_LM35DZ.Vout, C1.+, Arduino_Uno_and_Ethernet_shield.A0
  GND: T1_LM35DZ.GND, C1.-, Arduino_Uno_and_Ethernet_shield.GND
